// Logisim project 时钟.circ as structural Verilog: 1 circuit, main circuit main
module main (
  input  Clear
);

  wire and_1_out, clock_1_out, n74161_1_pin1, n74161_1_pin2, n74161_1_pin3, n74161_1_pin7, n74161_2_pin1,
       n74161_2_pin2, n74161_2_pin3, n74161_2_pin7, n74161_3_pin1, n74161_3_pin2, n74161_3_pin3,
       n74161_3_pin7, n74161_4_pin1, n74161_4_pin2, n74161_4_pin3, n74161_4_pin7, n74161_5_pin1,
       n74161_5_pin2, n74161_5_pin3, n74161_5_pin7, n74161_6_pin1, n74161_6_pin3, n74161_6_pin7, nand_1_out,
       nand_2_out;
  wire [3:0] n74161_1_pin14, n74161_2_pin14, n74161_3_pin14, n74161_4_pin14, n74161_5_pin14, n74161_6_pin14;

  _74161 u_74161_1 (
    .pin1(n74161_1_pin1), .pin2(n74161_1_pin2), .pin3(n74161_1_pin3), .pin4(n74161_1_pin3),
    .pin5(n74161_1_pin3), .pin6(n74161_1_pin3), .pin7(n74161_1_pin7), .pin14(n74161_1_pin14[0]),
    .pin13(n74161_1_pin14[1]), .pin12(n74161_1_pin14[2]), .pin11(n74161_1_pin14[3]), .pin10(n74161_1_pin7),
    .pin9(n74161_1_pin7));  // open: pin15
  nand nand_1 (nand_1_out, n74161_1_pin14[1], n74161_2_pin14[2]);
  _74161 u_74161_2 (
    .pin1(n74161_2_pin1), .pin2(n74161_2_pin2), .pin3(n74161_2_pin3), .pin4(n74161_2_pin3),
    .pin5(n74161_2_pin3), .pin6(n74161_2_pin3), .pin7(n74161_2_pin7), .pin14(n74161_2_pin14[0]),
    .pin13(n74161_2_pin14[1]), .pin12(n74161_2_pin14[2]), .pin11(n74161_2_pin14[3]), .pin10(n74161_2_pin7),
    .pin9(n74161_2_pin7));  // open: pin15
  and and_1 (and_1_out, nand_2_out, nand_1_out);
  nand nand_2 (nand_2_out, n74161_2_pin14[3], n74161_2_pin14[1]);
  not not_1 (n74161_1_pin2, nand_2_out);
  _74161 u_74161_3 (
    .pin1(n74161_3_pin1), .pin2(n74161_3_pin2), .pin3(n74161_3_pin3), .pin4(n74161_3_pin3),
    .pin5(n74161_3_pin3), .pin6(n74161_3_pin3), .pin7(n74161_3_pin7), .pin14(n74161_3_pin14[0]),
    .pin13(n74161_3_pin14[1]), .pin12(n74161_3_pin14[2]), .pin11(n74161_3_pin14[3]), .pin10(n74161_3_pin7),
    .pin9(n74161_3_pin7));  // open: pin15
  Hex_Digit_Display #(.decimalPoint("false")) hex_digit_display_1 (.value(n74161_1_pin14));
  Hex_Digit_Display #(.decimalPoint("false")) hex_digit_display_2 (.value(n74161_2_pin14));
  nand nand_3 (n74161_2_pin2, n74161_3_pin14[2], n74161_3_pin14[1]);
  Hex_Digit_Display #(.decimalPoint("false")) hex_digit_display_3 (.value(n74161_3_pin14));
  Hex_Digit_Display #(.decimalPoint("false")) hex_digit_display_4 (.value(n74161_4_pin14));
  _74161 u_74161_4 (
    .pin1(n74161_4_pin1), .pin2(n74161_4_pin2), .pin3(n74161_4_pin3), .pin4(n74161_4_pin3),
    .pin5(n74161_4_pin3), .pin6(n74161_4_pin3), .pin7(n74161_4_pin7), .pin14(n74161_4_pin14[0]),
    .pin13(n74161_4_pin14[1]), .pin12(n74161_4_pin14[2]), .pin11(n74161_4_pin14[3]), .pin10(n74161_4_pin7),
    .pin9(n74161_4_pin7));  // open: pin15
  Hex_Digit_Display #(.decimalPoint("false")) hex_digit_display_5 (.value(n74161_5_pin14));
  Hex_Digit_Display #(.decimalPoint("false")) hex_digit_display_6 (.value(n74161_6_pin14));
  nand nand_4 (n74161_3_pin2, n74161_4_pin14[3], n74161_4_pin14[1]);
  _74161 u_74161_5 (
    .pin1(n74161_5_pin1), .pin2(n74161_5_pin2), .pin3(n74161_5_pin3), .pin4(n74161_5_pin3),
    .pin5(n74161_5_pin3), .pin6(n74161_5_pin3), .pin7(n74161_5_pin7), .pin14(n74161_5_pin14[0]),
    .pin13(n74161_5_pin14[1]), .pin12(n74161_5_pin14[2]), .pin11(n74161_5_pin14[3]), .pin10(n74161_5_pin7),
    .pin9(n74161_5_pin7));  // open: pin15
  Clock clock_1 (.out(clock_1_out));
  nand nand_5 (n74161_4_pin2, n74161_5_pin14[2], n74161_5_pin14[1]);
  _74161 u_74161_6 (
    .pin1(n74161_6_pin1), .pin2(clock_1_out), .pin3(n74161_6_pin3), .pin4(n74161_6_pin3),
    .pin5(n74161_6_pin3), .pin6(n74161_6_pin3), .pin7(n74161_6_pin7), .pin14(n74161_6_pin14[0]),
    .pin13(n74161_6_pin14[1]), .pin12(n74161_6_pin14[2]), .pin11(n74161_6_pin14[3]), .pin10(n74161_6_pin7),
    .pin9(n74161_6_pin7));  // open: pin15
  and and_2 (n74161_6_pin1, Clear, n74161_5_pin2);
  nand nand_6 (n74161_5_pin2, n74161_6_pin14[3], n74161_6_pin14[1]);
  and and_3 (n74161_5_pin1, Clear, n74161_4_pin2);
  and and_4 (n74161_4_pin1, Clear, n74161_3_pin2);
  and and_5 (n74161_3_pin1, Clear, n74161_2_pin2);
  and and_6 (n74161_2_pin1, Clear, and_1_out);
  and and_7 (n74161_1_pin1, Clear, nand_1_out);
  // also tied to GND on the sheet: {n74161_1_pin3, n74161_2_pin3, n74161_3_pin3, n74161_4_pin3, n74161_5_pin3, n74161_6_pin3}
  // also tied to VCC on the sheet: {n74161_1_pin7, n74161_2_pin7, n74161_3_pin7, n74161_4_pin7, n74161_5_pin7, n74161_6_pin7}

  // Notes on the sheet:
  //   HOUR
  //   MINUTE
  //   :
  //   :
  //   SECOND
  //   Clock
  //   ©Devlin
endmodule
